// Logisim project clock24_complete.circ as structural Verilog: 3 circuits, main circuit main
module main (
  input  reset
);

  wire clock_1_out;
  wire [3:0] clock24_main_1_hour1, clock24_main_1_hour10, clock24_main_1_min1, clock24_main_1_min10;

  Clock clock_1 (.out(clock_1_out));
  Hex_Digit_Display hex_digit_display_1 (.value(clock24_main_1_hour10));  // open: dp
  clock24_main clock24_main_1 (
    .clock(clock_1_out), .reset(reset), .min1(clock24_main_1_min1), .min10(clock24_main_1_min10),
    .hour1(clock24_main_1_hour1), .hour10(clock24_main_1_hour10));
  Hex_Digit_Display hex_digit_display_2 (.value(clock24_main_1_hour1));  // open: dp
  Hex_Digit_Display hex_digit_display_3 (.value(clock24_main_1_min10));  // open: dp
  Hex_Digit_Display hex_digit_display_4 (.value(clock24_main_1_min1));  // open: dp
endmodule

module clock24_main (
  input  clock,
  input  reset,
  output [3:0] min1,
  output [3:0] min10,
  output [3:0] hour1,
  output [3:0] hour10
);

  wire and_1_out, and_2_out, counter_4bit_1_tc, counter_4bit_3_tc, or_1_out, or_2_out, or_3_out, or_4_out;

  or or_1 (or_1_out, reset, and_2_out);
  or or_2 (or_2_out, reset, and_1_out, and_2_out);
  or or_3 (or_3_out, reset, and_2_out);
  or or_4 (or_4_out, reset, and_2_out);
  counter_4bit counter_4bit_1 (
    .EN1(1'b1), .EN2(1'b1), .clock(clock), .reset(or_1_out), .Q0(min1[0]), .Q1(min1[1]), .Q2(min1[2]),
    .Q3(min1[3]), .TC(counter_4bit_1_tc));
  counter_4bit counter_4bit_2 (
    .EN1(counter_4bit_1_tc), .EN2(counter_4bit_1_tc), .clock(clock), .reset(or_2_out), .Q0(min10[0]),
    .Q1(min10[1]), .Q2(min10[2]), .Q3(min10[3]));  // open: TC
  counter_4bit counter_4bit_3 (
    .EN1(and_1_out), .EN2(and_1_out), .clock(clock), .reset(or_3_out), .Q0(hour1[0]), .Q1(hour1[1]),
    .Q2(hour1[2]), .Q3(hour1[3]), .TC(counter_4bit_3_tc));
  counter_4bit counter_4bit_4 (
    .EN1(counter_4bit_3_tc), .EN2(counter_4bit_3_tc), .clock(clock), .reset(or_4_out), .Q0(hour10[0]),
    .Q1(hour10[1]), .Q2(hour10[2]), .Q3(hour10[3]));  // open: TC
  and and_1 (and_1_out, min10[0], counter_4bit_1_tc, min10[2]);
  and and_2 (and_2_out, hour10[1], hour1[1], hour1[0], and_1_out);
endmodule

module counter_4bit (
  input  EN1,
  input  EN2,
  input  clock,
  input  reset,
  output Q0,
  output Q1,
  output Q2,
  output Q3,
  output TC
);

  wire and_1_out, and_2_out, and_3_out, and_4_out, and_5_out, and_6_out, and_7_out, and_8_out, and_9_out,
       and_10_out, and_11_out, and_12_out, B_qn, C_qn, D_qn, not_1_out, or_1_out, or_2_out, or_3_out,
       or_4_out, or_5_out;

  not not_1 (not_1_out, reset);
  and and_1 (and_1_out, 1'b1, EN2, EN1, not_1_out);
  and and_2 (and_2_out, Q2, EN2, EN1, reset);
  and and_3 (and_3_out, and_9_out, EN2, EN1, not_1_out);
  and and_4 (and_4_out, Q3, EN2, EN1, reset);
  and and_5 (and_5_out, and_10_out, EN2, EN1, not_1_out);
  and and_6 (and_6_out, Q0, EN2, EN1, reset);
  and and_7 (and_7_out, or_1_out, EN2, EN1, not_1_out);
  and and_8 (and_8_out, Q1, EN2, EN1, reset);
  or or_1 (or_1_out, and_11_out, and_12_out);
  or or_2 (or_2_out, and_1_out, and_2_out);
  or or_3 (or_3_out, and_3_out, and_4_out);
  or or_4 (or_4_out, and_5_out, and_6_out);
  or or_5 (or_5_out, and_7_out, and_8_out);
  and and_9 (and_9_out, D_qn, Q0);
  and and_10 (and_10_out, D_qn, Q1, Q0);
  and and_11 (and_11_out, Q3, C_qn, B_qn, Q0);
  and and_12 (and_12_out, D_qn, Q2, Q1, Q0);
  T_Flip_Flop A (.T(or_2_out), .clk(clock), .Q(Q0));  // open: Qn, reset, preset
  T_Flip_Flop B (.T(or_3_out), .clk(clock), .Q(Q1), .Qn(B_qn));  // open: reset, preset
  T_Flip_Flop C (.T(or_4_out), .clk(clock), .Q(Q2), .Qn(C_qn));  // open: reset, preset
  T_Flip_Flop D (.T(or_5_out), .clk(clock), .Q(Q3), .Qn(D_qn));  // open: reset, preset
  Hex_Digit_Display hex_digit_display_1 (.value({Q3, Q2, Q1, Q0}));  // open: dp
  and and_13 (TC, Q0, EN1, EN2, Q3);
endmodule
